# Fritzing sketch schematic (saved by Fritzing 0.9.3b)
breadboards: 1

parts:
  IC2 = Adafruit MAX31865 RTD Sensor Breakout [part_number=Max31865]
  U1 = Voltage Regulator - 3.3V [package="TO220 [THT]"]
  IC2_2 = Arduino Pro Mini (5V) [part_number="Arduino Pro Mini"]
  Q1 = Basic FET N-Channel [part_number=IRl-3803 package="TO220 [THT]"]
  Heating_Wire = Inductor [package="400 mil [THT]"]
  Lipo_3s = DC Power [voltage=12V]
  Pushbutton = Pushbutton [package="[THT]"]
  C1 = Electrolytic Capacitor [capacitance=470µF package="200 mil [THT, electrolytic]"]
  R2 = Resistor [tolerance=±5% resistance=10k package=THT]
  R3 = Resistor [tolerance=±5% resistance=220 package=THT]
  R4 = Resistor [tolerance=±5% resistance=10k package=THT]
  R5 = Resistor [tolerance=±5% resistance=33k package=THT]
  R6 = Resistor [tolerance=±5% resistance=10k package=THT]
  LED1 = LED - 3mm [color="Red (633nm)" package="3 mm [THT]"]
  R7 = Resistor [tolerance=±5% resistance=330 package=THT]

nets:
  VIN: IC2.VIN, IC2.3.3V, U1.output_voltage, IC2_2.VCC, Pushbutton.Pin_3, Pushbutton.Pin_4, C1.+
  GND: IC2.GND, U1.GND, IC2_2.GND, Q1.source, Lipo_3s.V-, C1.-, R2.Pin_1, R4.Pin_1, R6.Pin_1, LED1.cathode
  N1: IC2.SCLK, IC2_2.SCK
  N2: IC2.SDO, IC2_2.MISO
  N3: IC2.SDI, IC2_2.MOSI
  N4: IC2.CS, IC2_2.D10
  N5: U1.input_voltage, Heating_Wire.pin_0, Lipo_3s.V+, R5.Pin_0
  N6: IC2_2.A3, R5.Pin_1, R6.Pin_0
  N7: IC2_2.D6, R7.Pin_1
  N8: IC2_2.D5, R3.Pin_1
  N9: IC2_2.D3, Pushbutton.Pin_1, Pushbutton.Pin_2, R4.Pin_0
  N10: Q1.gate, R2.Pin_0, R3.Pin_0
  N11: Q1.drain, Heating_Wire.pin_1
  N12: LED1.anode, R7.Pin_0

custom parts:
  Adafruit MAX31865 RTD Sensor Breakout: For precision temperature sensing, nothing beats a Platinum RTD. Resistance temperature detectors (RTDs) are temperature sensors that contain a resistor that changes resistance value as its temperature changes, basically a kind of thermistor. In this sensor, the resistor is actually a small strip of Platinum with a resistance of 100 ohms at 0°C, thus the name PT100. Compared to most NTC/PTC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
